# Fritzing sketch Temperature_logger_scematics (saved by Fritzing 0.9.3b)

parts:
  Part1 = MicroSD Card Module
  Part2 = Arduino Uno (Rev3) - ICSP
  T1 = TMP36 Temperature Sensor [package="TO92 [THT]"]

nets:
  GND: Part1.GND, Part2.GND, T1.GND
  VCC: Part1.VCC, Part2.5V, T1.+Vs
  N1: Part1.MISO, Part2.ICSP_MISO, Part2.D12/MISO
  N2: Part1.MOSI, Part2.D11_PWM/MOSI
  N3: Part1.SCK, Part2.D13/SCK
  N4: Part1.CS, Part2.D10_PWM/SS
  N5: Part2.A0, T1.Vout
